# Fritzing sketch PowerBtn (saved by Fritzing 0.9.2b)
breadboards: 1

parts:
  U1 = attiny85 [package=dip]
  X1 = USB Connectors [package=usb-a-h]
  R1 = Resistor [tolerance=±5% resistance=68 package=THT]
  R2 = Resistor [tolerance=±5% resistance=68 package=THT]
  R3 = Resistor [tolerance=±5% resistance=1.5k package=THT]
  D1 = Zener Diode [part_number=1N4732A breakdown_voltage=3.6V package="Melf DO-213 AB [SMD]"]
  D2 = Zener Diode [part_number=1N4732A breakdown_voltage=3.6V package="Melf DO-213 AB [SMD]"]
  C1 = Electrolytic Capacitor [capacitance=1µF package="100 mil [THT, electrolytic]"]

nets:
  to PowerCtrl: U1.Pin_2
  GND: U1.Pin_4, X1.GND, D1.anode, D2.anode, C1.-
  N1: U1.Pin_5, R2.Pin_0
  N2: U1.Pin_7, R1.Pin_0
  5V: U1.Pin_8, X1.D+, R3.Pin_1, C1.+
  N3: X1.D-, R2.Pin_1, R3.Pin_0, D2.cathode
  N4: X1.VBUS, R1.Pin_1, D1.cathode

notes:
  PowerBtn, 1.0
