# Fritzing sketch PowerCtrl (saved by Fritzing 0.9.2b)
breadboards: 1

parts:
  U1 = attiny85 [package=dip]
  R2 = Resistor [tolerance=±5% resistance=10k package=THT]
  R1 = PHOTOCELL [package=photocell]
  R3 = Trimmer Potentiometer [maximum_resistance=10kΩ package=THT]
  C1 = Electrolytic Capacitor [capacitance=10µF package="100 mil [THT, electrolytic]"]
  S1 = Pushbutton [package=THT]
  D1 = Schottky Diode [part_number=1N5817 package="300 mil [THT]"]
  R4 = Resistor [tolerance=±5% resistance=1k package=THT]
  LED1 = LEDs [package=led10mm]
  D2 = Schottky Diode [part_number=1N5817 package="Melf DO-213 AB [SMD]"]

nets:
  N1: U1.Pin_2, R2.Pin_0, R1.P$2
  N2: U1.Pin_3, D1.anode
  GND: U1.Pin_4, R1.P$1, C1.-, S1.leg0, LED1.C
  Output: U1.Pin_5
  N3: U1.Pin_7, R4.Pin_0
  5V: U1.Pin_8, R3.leg2
  N4: R2.Pin_1, R3.leg1, R3.wiper
  N5: S1.leg1, D1.cathode, D2.cathode
  N6: R4.Pin_1, LED1.A
  to PowerBtn: D2.anode

notes:
  PowerCtrl, 1.3
